# Fritzing sketch Tumbglove (saved by Fritzing 0.7.11b)
breadboards: 1

parts:
  Arduino1 = Arduino
  R2 = Resistor [tolerance=±5% resistance=10k package=THT]
  R1 = Basic Flex Resistor
  IC1 = SO08 [chip_label=KXM52-1050 package=SO]

nets:
  N1: Arduino1.GND, Arduino1.A0, R2.Pin_0, R2.Pin_1, R1.pin_1
  N2: Arduino1.+5V, R1.Pin_2, IC1.1, IC1.2, IC1.5
  N3: Arduino1.A2, IC1.6
  N4: Arduino1.A3, IC1.7
  N5: Arduino1.A4, IC1.8

notes:
  ARDUINO
  LEONARDO
